// Digital circuit simple cpu.dig as structural Verilog
module simple_cpu (
  input  DMAreq,
  input  Nmi,
  input  Int,
  input  R,
  input  Clk,
  output [7:0] D,
  output [15:0] Adr,
  output DMAack,
  output Sync,
  output W_nR,
  output BEn,
  output IntAck
);

  wire A2Alu, A2DBus, ABufLoad, ACBALoad, ACBBLoad, ACRes2ACB, ACRes2HLBus, add_1_c_o, ALoad, Alu2Flags,
       and_1_out, and_2_out, and_3_out, and_4_out, and_6_out, and_7_out, and_10_out, and_14_out, and_15_out,
       and_16_out, and_17_out, and_18_out, and_19_out, and_20_out, and_21_out, and_22_out, and_23_out,
       and_24_out, and_25_out, and_26_out, and_27_out, and_28_out, and_29_out, and_30_out, and_31_out,
       and_32_out, and_33_out, and_34_out, and_35_out, and_36_out, and_37_out, and_38_out, and_39_out,
       and_40_out, and_41_out, and_42_out, and_43_out, and_44_out, and_45_out, and_46_out, and_47_out, AOut,
       ATemp2ABus, ATempLoad, ClearExInstFlag, DBuf2DBus, DBufLoad, DBufOut, DBus2A, DBus2DBuf, DBus2Flags,
       DBus2HLBus, DBus2HLBusSel, DBus2Temp, decoder_2_out_1, decoder_4_out_0, decoder_5_out_1,
       decoder_5_out_2, decoder_5_out_3, decoder_5_out_4, decoder_5_out_5, decoder_6_out_1, decoder_6_out_2,
       decoder_6_out_3, decoder_6_out_4, decoder_6_out_5, decoder_7_out_1, decoder_7_out_2, decoder_7_out_3,
       decoder_7_out_4, decoder_7_out_5, decoder_8_out_1, decoder_8_out_2, decoder_8_out_3, decoder_8_out_4,
       decoder_8_out_5, Execute2Fetch, ExecutePhase, ExtIntOverride, Fetch2Execute, FetchPhase, Flags2Alu,
       Flags2DBus, HBus2Reg0, HBus2Reg1, HLBus2DBus, HLBus2DBusSel, Imm2ABus, Imm2BBus, Imm2DBus,
       InterruptRequest, LBus2Reg0, LBus2Reg1, LoadCarryFlag, LoadInterrupEnableFlag, LoadSignFlag,
       LoadZeroFlag, or_3_out, or_4_out, PhaseChangeReq, RBus2DBus, Reg02HBus, Reg02LBus, Reg12HBus,
       Reg12LBus, SetExInstFlag, SpecialRegSet0, SpecialRegSet1, SpecialRegSet2, SpecialRegSet3, sub_1_c_o,
       Temp2Alu, Temp2DBus, TempLoad, TempOut, TogglePhase;
  wire [0:0] pulldown_1_out;
  wire [1:0] AckSel, ACOp, Imm2BusSel, priorityencoder_1_num, priorityencoder_2_num, SpecialRegSetSel;
  wire [2:0] AluOp, DBusSourceSel, HBus2RegSel, LBus2RegSel, multiplexer_2_out, Reg2HBusSel, Reg2LBusSel;
  wire [2:2] Fetch_Management_Code_Low_d;
  wire [3:0] add_2_s;
  wire [4:0] Flags;
  wire [7:0] ABusVal, add_1_s, and_5_out, ATempVal, Aux1hVal, Aux1lVal, Aux2hVal, Aux2lVal, Aux3hVal,
       Aux3lVal, AVal, BBusVal, BVal, counterpreset_1_out, CVal, DBufVal, DBusVal, driver_1_out,
       driver_2_out, driver_7_out, driver_12_out, driver_15_out, driver_20_out, driver_24_out, driver_31_out,
       driver_32_out, driverinvsel_1_out, driverinvsel_3_out, DVal, EVal, HBusVal, HVal, Imm, IRVal, IVhVal,
       IVlVal, IXhVal, IXlVal, IYhVal, IYlVal, LBusVal, LRhVal, LRlVal, LVal, multiplexer_4_out, not_1_out,
       or_1_out, PChVal, PClVal, RBusVal, SPhVal, SPlVal, sub_1_s, TempVal, WVal, xor_1_out, ZVal;
  wire [15:0] ABufVal, ACB_A_q, ACB_B_q, add_3_s, add_4_s, add_5_s, bitextender_1_out, driverinvsel_4_out,
       multiplexer_5_out, sub_2_s;
  wire [16:0] McAddrVal, multiplexer_3_out;
  wire [31:1] Fetch_Management_Code_Extended_d;

  assign driver_1_out = DBus2A ? DBusVal : 8'bz;  // Driver driver_1
  Register #(.Bits(8)) A (.D(driver_1_out), .C(Clk), .en(ALoad), .Q(AVal));
  assign driverinvsel_1_out = ~AOut ? driver_1_out : 8'bz;  // DriverInvSel driverinvsel_1
  assign driver_2_out = A2Alu ? driverinvsel_1_out : 8'bz;  // Driver driver_2
  assign ABusVal = ~ATemp2ABus ? driver_2_out : 8'bz;  // DriverInvSel driverinvsel_2
  assign ABusVal = Imm2ABus ? Imm : 8'bz;  // Driver driver_3
  Register #(.Bits(8)) A_Temp (.D(driver_2_out), .C(Clk), .en(ATempLoad), .Q(ATempVal));
  assign DBusVal = A2DBus ? driverinvsel_1_out : 8'bz;  // Driver driver_4
  assign driverinvsel_1_out = AOut ? AVal : 8'bz;  // Driver driver_5
  assign ABusVal = ATemp2ABus ? ATempVal : 8'bz;  // Driver driver_6
  assign driver_7_out = DBus2Temp ? DBusVal : 8'bz;  // Driver driver_7
  assign driverinvsel_3_out = ~TempOut ? driver_7_out : 8'bz;  // DriverInvSel driverinvsel_3
  Register #(.Bits(8)) Temp (.D(driver_7_out), .C(Clk), .en(TempLoad), .Q(TempVal));
  assign BBusVal = Temp2Alu ? driverinvsel_3_out : 8'bz;  // Driver driver_8
  assign BBusVal = Imm2BBus ? Imm : 8'bz;  // Driver driver_9
  assign driverinvsel_3_out = TempOut ? TempVal : 8'bz;  // Driver driver_10
  assign DBusVal = Temp2DBus ? driverinvsel_3_out : 8'bz;  // Driver driver_11
  assign driver_12_out = DBus2Flags ? DBusVal : 8'bz;  // Driver driver_12
  assign driver_12_out = Alu2Flags ? {{5{1'b0}}, multiplexer_2_out[2], RBusVal[7], multiplexer_2_out[0]} : 8'bz;  // Driver driver_13
  PullDown pulldown_1 (.out(pulldown_1_out[0]));
  and and_1 (and_1_out, Clk, LoadZeroFlag);
  and and_2 (and_2_out, Clk, LoadSignFlag);
  and and_3 (and_3_out, Clk, LoadCarryFlag);
  and and_4 (and_4_out, Clk, LoadInterrupEnableFlag);
  D_FF d_ff_1 (.D(driver_12_out[0]), .C(and_1_out), .Q(Flags[0]));  // open: nQ
  D_FF d_ff_2 (.D(driver_12_out[1]), .C(and_2_out), .Q(Flags[1]));  // open: nQ
  D_FF d_ff_3 (.D(driver_12_out[2]), .C(and_3_out), .Q(Flags[2]));  // open: nQ
  D_FF d_ff_4 (.D(driver_12_out[3]), .C(and_4_out), .Q(Flags[3]));  // open: nQ
  RS_FF_AS rs_ff_as_1 (.S(SetExInstFlag), .R(ClearExInstFlag), .Q(Flags[4]));  // open: nQ
  assign and_5_out = ABusVal & BBusVal;  // And and_5, 8 bits wide
  assign or_1_out = ABusVal | BBusVal;  // Or or_1, 8 bits wide
  assign not_1_out = ~ABusVal;  // Not not_1, 8 bits wide
  assign xor_1_out = ABusVal ^ BBusVal;  // XOr xor_1, 8 bits wide
  Add #(.Bits(8)) add_1 (.a(ABusVal), .b(BBusVal), .c_i(pulldown_1_out[0]), .s(add_1_s), .c_o(add_1_c_o));
  Sub #(.Bits(8)) sub_1 (.a(ABusVal), .b(BBusVal), .c_i(pulldown_1_out[0]), .s(sub_1_s), .c_o(sub_1_c_o));
  Multiplexer #(.Selector_Bits(3), .Bits(8)) multiplexer_1 (
    .sel(AluOp), .in_0(and_5_out), .in_1(or_1_out), .in_2(not_1_out), .in_3(xor_1_out),
    .in_4({ABusVal[6:0], pulldown_1_out[0]}), .in_5({pulldown_1_out[0], ABusVal[7:1]}), .in_6(add_1_s),
    .in_7(sub_1_s), .out(RBusVal));
  LED Z (.in(Flags[0]));
  LED S (.in(Flags[1]));
  LED C (.in(Flags[2]));
  LED IE (.in(Flags[3]));
  LED ExInst (.in(Flags[4]));
  assign DBusVal = Flags2DBus ? {3'b000, Flags} : 8'bz;  // Driver driver_14
  assign {driver_15_out[7:3], pulldown_1_out[0], driver_15_out[1:0]} = Flags2Alu ? {3'b000, Flags} : 8'bz;  // Driver driver_15
  Multiplexer #(.Selector_Bits(3)) multiplexer_2 (
    .sel(AluOp), .in_0(1'b0), .in_1(1'b0), .in_2(1'b0), .in_3(1'b0), .in_4(ABusVal[7]), .in_5(ABusVal[0]),
    .in_6(add_1_c_o), .in_7(sub_1_c_o), .out(multiplexer_2_out[2]));
  nor nor_1 (multiplexer_2_out[0], RBusVal[7], RBusVal[7], RBusVal[6], RBusVal[5], RBusVal[4], RBusVal[3], RBusVal[2], RBusVal[1], RBusVal[0]);
  // Probe on DBusVal
  // Probe on AVal
  // Probe on ATempVal
  // Probe on BBusVal
  // Probe on ABusVal
  // Probe on DBufVal
  // Probe on ABufVal
  CounterPreset #(.Bits(8)) counterpreset_1 (
    .en(1'b1), .C(Clk), .dir(1'b0), .in({8{1'b0}}), .ld(1'b0), .clr(1'b0), .out(counterpreset_1_out));  // open: ovf
  // Probe on counterpreset_1_out
  assign DBusVal = RBus2DBus ? RBusVal : 8'bz;  // Driver driver_16
  LED Fetch (.in(FetchPhase));
  LED Execute (.in(ExecutePhase));
  // Probe on TempVal
  // Probe on RBusVal
  // Probe on IRVal
  // Probe on {McAddrVal[16:12], IRVal, McAddrVal[3:0]}
  // Probe on HBusVal
  // Probe on LBusVal
  // Probe on WVal
  // Probe on BVal
  // Probe on DVal
  // Probe on HVal
  // Probe on SPhVal
  // Probe on PChVal
  // Probe on LRhVal
  // Probe on IXhVal
  // Probe on IYhVal
  // Probe on IVhVal
  and and_6 (and_6_out, Flags[3], Int);
  Decoder #(.Selector_Bits(3)) decoder_1 (
    .sel(DBusSourceSel), .out_1(Imm2DBus), .out_2(Flags2DBus), .out_3(RBus2DBus), .out_4(Temp2DBus),
    .out_5(A2DBus), .out_6(DBuf2DBus), .out_7(HLBus2DBus));  // open: out_0
  Decoder #(.Selector_Bits(2)) decoder_2 (
    .sel(Imm2BusSel), .out_1(decoder_2_out_1), .out_2(Imm2ABus), .out_3(Imm2BBus));  // open: out_0
  Decoder #(.Selector_Bits(2)) decoder_3 (
    .sel(SpecialRegSetSel), .out_0(SpecialRegSet0), .out_1(SpecialRegSet1), .out_2(SpecialRegSet2),
    .out_3(SpecialRegSet3));
  Decoder #(.Selector_Bits(2)) decoder_4 (
    .sel(AckSel), .out_0(decoder_4_out_0), .out_1(IntAck), .out_2(DMAack), .out_3(Sync));
  or or_2 (InterruptRequest, and_6_out, Nmi);
  // Probe on ZVal
  // Probe on CVal
  // Probe on EVal
  // Probe on LVal
  // Probe on SPlVal
  // Probe on PClVal
  // Probe on LRlVal
  // Probe on IXlVal
  // Probe on IYlVal
  // Probe on IVlVal
  PriorityEncoder #(.Selector_Bits(2)) priorityencoder_1 (
    .in0(1'b1), .in1(InterruptRequest), .in2(R), .in3(1'b0), .num(priorityencoder_1_num));  // open: any
  T_FF Fetch_Exec (.T(TogglePhase), .C(Clk), .Q(ExecutePhase), .nQ(FetchPhase));
  or or_3 (or_3_out, ExtIntOverride, Fetch2Execute);
  Add #(.Bits(4)) add_2 (.a(McAddrVal[3:0]), .b(4'b0001), .c_i(1'b0), .s(add_2_s));  // open: c_o
  and and_7 (and_7_out, Clk, W_nR);
  PriorityEncoder #(.Selector_Bits(2)) priorityencoder_2 (
    .in0(1'b1), .in1(Execute2Fetch), .in2(or_3_out), .in3(1'b0), .num(priorityencoder_2_num));  // open: any
  EEPROM #(.AddrBits(16), .Bits(8)) eeprom_1 (.A(Adr), .CS(BEn), .WE(and_7_out), .OE(~W_nR), .D(D));
  Multiplexer #(.Selector_Bits(2), .Bits(17)) multiplexer_3 (
    .sel(priorityencoder_2_num), .in_0({Flags, IRVal, add_2_s}),
    .in_1({{11{1'b0}}, priorityencoder_1_num, 4'b0000}), .in_2({Flags, DBusVal, 4'b0000}), .in_3({17{1'b0}}),
    .out(multiplexer_3_out));
  assign DBusVal = Imm2DBus ? Imm : 8'bz;  // Driver driver_17
  Register #(.Bits(17)) MCAdr (
    .D(multiplexer_3_out), .C(Clk), .en(1'b1), .Q({McAddrVal[16:12], IRVal, McAddrVal[3:0]}));
  and and_8 (Execute2Fetch, TogglePhase, ExecutePhase);
  and and_9 (Fetch2Execute, TogglePhase, FetchPhase);
  ROM #(.AddrBits(17), .Bits(32)) Fetch_Management_Code_High (
    .A({McAddrVal[16:12], IRVal, McAddrVal[3:0]}), .sel(FetchPhase),
    .D({SpecialRegSetSel, Imm2BusSel, Imm, DBusSourceSel, LBus2RegSel, Reg2LBusSel, HBus2RegSel, Reg2HBusSel, DBus2HLBusSel, HLBus2DBusSel, ATemp2ABus, ATempLoad, Flags2Alu}));
  ROM #(.AddrBits(17), .Bits(32)) Fetch_Management_Code_Low (
    .A({McAddrVal[16:12], IRVal, McAddrVal[3:0]}), .sel(FetchPhase),
    .D({Alu2Flags, LoadInterrupEnableFlag, LoadCarryFlag, LoadSignFlag, LoadZeroFlag, ACRes2ACB, ABufLoad, DBufLoad, DBufOut, ACRes2HLBus, ACOp, DBus2Temp, DBus2Flags, DBus2DBuf, DBus2A, DBus2HLBus, ACBBLoad, ACBALoad, Temp2Alu, TempLoad, TempOut, A2Alu, ALoad, AOut, AluOp, PhaseChangeReq, Fetch_Management_Code_Low_d[2], BEn, W_nR}));
  ROM #(.AddrBits(17), .Bits(32)) Fetch_Management_Code_Extended (
    .A({McAddrVal[16:12], IRVal, McAddrVal[3:0]}), .sel(FetchPhase),
    .D({Fetch_Management_Code_Extended_d[31:4], AckSel, Fetch_Management_Code_Extended_d[1], SetExInstFlag}));
  ROM #(.AddrBits(17), .Bits(32)) Execute_Code_High (
    .A({McAddrVal[16:12], IRVal, McAddrVal[3:0]}), .sel(ExecutePhase),
    .D({SpecialRegSetSel, Imm2BusSel, Imm, DBusSourceSel, LBus2RegSel, Reg2LBusSel, HBus2RegSel, Reg2HBusSel, DBus2HLBusSel, HLBus2DBusSel, ATemp2ABus, ATempLoad, Flags2Alu}));
  ROM #(.AddrBits(17), .Bits(32)) Execute_Code_Low (
    .A({McAddrVal[16:12], IRVal, McAddrVal[3:0]}), .sel(ExecutePhase),
    .D({Alu2Flags, LoadInterrupEnableFlag, LoadCarryFlag, LoadSignFlag, LoadZeroFlag, ACRes2ACB, ABufLoad, DBufLoad, DBufOut, ACRes2HLBus, ACOp, DBus2Temp, DBus2Flags, DBus2DBuf, DBus2A, DBus2HLBus, ACBBLoad, ACBALoad, Temp2Alu, TempLoad, TempOut, A2Alu, ALoad, AOut, AluOp, PhaseChangeReq, Fetch_Management_Code_Low_d[2], BEn, W_nR}));
  ROM #(.AddrBits(17), .Bits(32)) Execute_Code_Extended (
    .A({McAddrVal[16:12], IRVal, McAddrVal[3:0]}), .sel(ExecutePhase),
    .D({Fetch_Management_Code_Extended_d[31:4], AckSel, Fetch_Management_Code_Extended_d[1], SetExInstFlag}));
  or or_4 (or_4_out, DBuf2DBus, DBufLoad);
  and and_10 (and_10_out, or_4_out, ~W_nR, ~DBufOut);  // And
  assign D = W_nR ? driver_20_out : 8'bz;  // Driver driver_18
  Register #(.Bits(8)) D_Buffer (.D(driver_20_out), .C(Clk), .en(DBufLoad), .Q(DBufVal));
  assign DBusVal = DBuf2DBus ? driver_20_out : 8'bz;  // Driver driver_19
  assign driver_20_out = and_10_out ? D : 8'bz;  // Driver driver_20
  and and_11 (TogglePhase, PhaseChangeReq, ~ExtIntOverride);  // And
  and and_12 (ExtIntOverride, SetExInstFlag, PhaseChangeReq);
  and and_13 (ClearExInstFlag, ~SetExInstFlag, ExecutePhase, PhaseChangeReq);  // And
  assign driver_20_out = DBufOut ? DBufVal : 8'bz;  // Driver driver_21
  assign driver_20_out = DBus2DBuf ? DBusVal : 8'bz;  // Driver driver_22
  Decoder #(.Selector_Bits(3)) decoder_5 (
    .sel(Reg2HBusSel), .out_1(decoder_5_out_1), .out_2(decoder_5_out_2), .out_3(decoder_5_out_3),
    .out_4(decoder_5_out_4), .out_5(decoder_5_out_5), .out_6(Reg02HBus), .out_7(Reg12HBus));  // open: out_0
  Decoder #(.Selector_Bits(3)) decoder_6 (
    .sel(HBus2RegSel), .out_1(decoder_6_out_1), .out_2(decoder_6_out_2), .out_3(decoder_6_out_3),
    .out_4(decoder_6_out_4), .out_5(decoder_6_out_5), .out_6(HBus2Reg0), .out_7(HBus2Reg1));  // open: out_0
  Register #(.Bits(8)) W (.D(HBusVal), .C(Clk), .en(decoder_6_out_1), .Q(WVal));
  Register #(.Bits(8)) B (.D(HBusVal), .C(Clk), .en(decoder_6_out_2), .Q(BVal));
  Register #(.Bits(8)) u_D (.D(HBusVal), .C(Clk), .en(decoder_6_out_3), .Q(DVal));
  Register #(.Bits(8)) H (.D(HBusVal), .C(Clk), .en(decoder_6_out_4), .Q(HVal));
  Register #(.Bits(8)) SPh (.D(HBusVal), .C(Clk), .en(decoder_6_out_5), .Q(SPhVal));
  assign DBusVal = HLBus2DBus ? multiplexer_4_out : 8'bz;  // Driver driver_23
  Multiplexer #(.Bits(8)) multiplexer_4 (
    .sel(HLBus2DBusSel), .in_0(driver_24_out), .in_1(driver_31_out), .out(multiplexer_4_out));
  assign driver_24_out = HLBus2DBus ? LBusVal : 8'bz;  // Driver driver_24
  assign HBusVal = decoder_5_out_1 ? WVal : 8'bz;  // Driver driver_25
  assign HBusVal = decoder_5_out_2 ? BVal : 8'bz;  // Driver driver_26
  assign HBusVal = decoder_5_out_3 ? DVal : 8'bz;  // Driver driver_27
  assign HBusVal = decoder_5_out_4 ? HVal : 8'bz;  // Driver driver_28
  assign HBusVal = decoder_5_out_5 ? SPhVal : 8'bz;  // Driver driver_29
  PullDown #(.Bits(8)) pulldown_2 (.out(HBusVal));
  assign LBusVal = and_15_out ? driver_32_out : 8'bz;  // Driver driver_30
  assign driver_31_out = HLBus2DBus ? HBusVal : 8'bz;  // Driver driver_31
  assign driverinvsel_4_out = ~ACRes2ACB ? {HBusVal, LBusVal} : 16'bz;  // DriverInvSel driverinvsel_4
  assign driver_32_out = DBus2HLBus ? DBusVal : 8'bz;  // Driver driver_32
  assign HBusVal = and_14_out ? driver_32_out : 8'bz;  // Driver driver_33
  assign LBusVal = decoder_7_out_1 ? ZVal : 8'bz;  // Driver driver_34
  assign LBusVal = decoder_7_out_2 ? CVal : 8'bz;  // Driver driver_35
  assign LBusVal = decoder_7_out_3 ? EVal : 8'bz;  // Driver driver_36
  assign LBusVal = decoder_7_out_4 ? LVal : 8'bz;  // Driver driver_37
  assign LBusVal = decoder_7_out_5 ? SPlVal : 8'bz;  // Driver driver_38
  PullDown #(.Bits(8)) pulldown_3 (.out(LBusVal));
  Register #(.Bits(16)) ACB_A (.D(driverinvsel_4_out), .C(Clk), .en(ACBALoad), .Q(ACB_A_q));
  Register #(.Bits(16)) ACB_B (.D(driverinvsel_4_out), .C(Clk), .en(ACBBLoad), .Q(ACB_B_q));
  Register #(.Bits(16)) A_Buffer (.D(driverinvsel_4_out), .C(Clk), .en(ABufLoad), .Q(ABufVal));
  Register #(.Bits(8)) Z_2 (.D(LBusVal), .C(Clk), .en(decoder_8_out_1), .Q(ZVal));
  Register #(.Bits(8)) C_2 (.D(LBusVal), .C(Clk), .en(decoder_8_out_2), .Q(CVal));
  Register #(.Bits(8)) E (.D(LBusVal), .C(Clk), .en(decoder_8_out_3), .Q(EVal));
  Register #(.Bits(8)) L (.D(LBusVal), .C(Clk), .en(decoder_8_out_4), .Q(LVal));
  Register #(.Bits(8)) SPl (.D(LBusVal), .C(Clk), .en(decoder_8_out_5), .Q(SPlVal));
  assign Adr = BEn ? ABufVal : 16'bz;  // Driver driver_39
  and and_14 (and_14_out, DBus2HLBus, DBus2HLBusSel);
  and and_15 (and_15_out, DBus2HLBus, ~DBus2HLBusSel);  // And
  BitExtender bitextender_1 (.in(ACB_B_q[7:0]), .out(bitextender_1_out));
  assign driverinvsel_4_out = ACRes2ACB ? multiplexer_5_out : 16'bz;  // Driver driver_40
  Add #(.Bits(16)) add_3 (.a(ACB_A_q), .b(16'h1), .c_i(1'b0), .s(add_3_s));  // open: c_o
  Add #(.Bits(16)) add_4 (.a(ACB_A_q), .b(ACB_B_q), .c_i(1'b0), .s(add_4_s));  // open: c_o
  Add #(.Bits(16)) add_5 (.a(ACB_A_q), .b(bitextender_1_out), .c_i(1'b0), .s(add_5_s));  // open: c_o
  Sub #(.Bits(16)) sub_2 (.a(ACB_A_q), .b(16'h1), .c_i(1'b0), .s(sub_2_s));  // open: c_o
  Decoder #(.Selector_Bits(3)) decoder_7 (
    .sel(Reg2LBusSel), .out_1(decoder_7_out_1), .out_2(decoder_7_out_2), .out_3(decoder_7_out_3),
    .out_4(decoder_7_out_4), .out_5(decoder_7_out_5), .out_6(Reg02LBus), .out_7(Reg12LBus));  // open: out_0
  Decoder #(.Selector_Bits(3)) decoder_8 (
    .sel(LBus2RegSel), .out_1(decoder_8_out_1), .out_2(decoder_8_out_2), .out_3(decoder_8_out_3),
    .out_4(decoder_8_out_4), .out_5(decoder_8_out_5), .out_6(LBus2Reg0), .out_7(LBus2Reg1));  // open: out_0
  Multiplexer #(.Selector_Bits(2), .Bits(16)) multiplexer_5 (
    .sel(ACOp), .in_0(add_3_s), .in_1(add_4_s), .in_2(add_5_s), .in_3(sub_2_s), .out(multiplexer_5_out));
  assign {HBusVal, LBusVal} = ACRes2HLBus ? multiplexer_5_out : 16'bz;  // Driver driver_41
  and and_16 (and_16_out, Reg02HBus, SpecialRegSet0);
  and and_17 (and_17_out, HBus2Reg0, SpecialRegSet0);
  and and_18 (and_18_out, Reg12HBus, SpecialRegSet0);
  and and_19 (and_19_out, HBus2Reg1, SpecialRegSet0);
  and and_20 (and_20_out, Reg02HBus, SpecialRegSet2);
  and and_21 (and_21_out, HBus2Reg0, SpecialRegSet2);
  and and_22 (and_22_out, Reg12HBus, SpecialRegSet2);
  and and_23 (and_23_out, HBus2Reg1, SpecialRegSet2);
  Register #(.Bits(8)) PCh (.D(HBusVal), .C(Clk), .en(and_17_out), .Q(PChVal));
  Register #(.Bits(8)) LRh (.D(HBusVal), .C(Clk), .en(and_19_out), .Q(LRhVal));
  Register #(.Bits(8)) IVh (.D(HBusVal), .C(Clk), .en(and_21_out), .Q(IVhVal));
  Register #(.Bits(8)) Aux3h (.D(HBusVal), .C(Clk), .en(and_23_out), .Q(Aux3hVal));
  assign HBusVal = and_16_out ? PChVal : 8'bz;  // Driver driver_42
  assign HBusVal = and_18_out ? LRhVal : 8'bz;  // Driver driver_43
  assign HBusVal = and_20_out ? IVhVal : 8'bz;  // Driver driver_44
  assign HBusVal = and_22_out ? Aux3hVal : 8'bz;  // Driver driver_45
  Register #(.Bits(8)) PCl (.D(LBusVal), .C(Clk), .en(and_24_out), .Q(PClVal));
  assign LBusVal = and_25_out ? PClVal : 8'bz;  // Driver driver_46
  Register #(.Bits(8)) LRl (.D(LBusVal), .C(Clk), .en(and_26_out), .Q(LRlVal));
  assign LBusVal = and_27_out ? LRlVal : 8'bz;  // Driver driver_47
  Register #(.Bits(8)) IVl (.D(LBusVal), .C(Clk), .en(and_28_out), .Q(IVlVal));
  assign LBusVal = and_29_out ? IVlVal : 8'bz;  // Driver driver_48
  Register #(.Bits(8)) Aux3l (.D(LBusVal), .C(Clk), .en(and_30_out), .Q(Aux3lVal));
  assign LBusVal = and_31_out ? Aux3lVal : 8'bz;  // Driver driver_49
  and and_24 (and_24_out, SpecialRegSet0, LBus2Reg0);
  and and_25 (and_25_out, SpecialRegSet0, Reg02LBus);
  and and_26 (and_26_out, SpecialRegSet0, LBus2Reg1);
  and and_27 (and_27_out, SpecialRegSet0, Reg12LBus);
  and and_28 (and_28_out, SpecialRegSet2, LBus2Reg0);
  and and_29 (and_29_out, SpecialRegSet2, Reg02LBus);
  and and_30 (and_30_out, SpecialRegSet2, LBus2Reg1);
  and and_31 (and_31_out, SpecialRegSet2, Reg12LBus);
  and and_32 (and_32_out, Reg02HBus, SpecialRegSet1);
  and and_33 (and_33_out, HBus2Reg0, SpecialRegSet1);
  and and_34 (and_34_out, Reg12HBus, SpecialRegSet1);
  and and_35 (and_35_out, HBus2Reg1, SpecialRegSet1);
  and and_36 (and_36_out, Reg02HBus, SpecialRegSet3);
  and and_37 (and_37_out, HBus2Reg0, SpecialRegSet3);
  and and_38 (and_38_out, Reg12HBus, SpecialRegSet3);
  and and_39 (and_39_out, HBus2Reg1, SpecialRegSet3);
  Register #(.Bits(8)) IXh (.D(HBusVal), .C(Clk), .en(and_33_out), .Q(IXhVal));
  Register #(.Bits(8)) IYh (.D(HBusVal), .C(Clk), .en(and_35_out), .Q(IYhVal));
  Register #(.Bits(8)) Aux1h (.D(HBusVal), .C(Clk), .en(and_37_out), .Q(Aux1hVal));
  Register #(.Bits(8)) Aux2h (.D(HBusVal), .C(Clk), .en(and_39_out), .Q(Aux2hVal));
  assign HBusVal = and_32_out ? IXhVal : 8'bz;  // Driver driver_50
  assign HBusVal = and_34_out ? IYhVal : 8'bz;  // Driver driver_51
  assign HBusVal = and_36_out ? Aux1hVal : 8'bz;  // Driver driver_52
  assign HBusVal = and_38_out ? Aux2hVal : 8'bz;  // Driver driver_53
  Register #(.Bits(8)) IXl (.D(LBusVal), .C(Clk), .en(and_40_out), .Q(IXlVal));
  assign LBusVal = and_41_out ? IXlVal : 8'bz;  // Driver driver_54
  Register #(.Bits(8)) IYl (.D(LBusVal), .C(Clk), .en(and_42_out), .Q(IYlVal));
  assign LBusVal = and_43_out ? IYlVal : 8'bz;  // Driver driver_55
  Register #(.Bits(8)) Aux1l (.D(LBusVal), .C(Clk), .en(and_44_out), .Q(Aux1lVal));
  assign LBusVal = and_45_out ? Aux1lVal : 8'bz;  // Driver driver_56
  Register #(.Bits(8)) Aux2l (.D(LBusVal), .C(Clk), .en(and_46_out), .Q(Aux2lVal));
  assign LBusVal = and_47_out ? Aux2lVal : 8'bz;  // Driver driver_57
  and and_40 (and_40_out, SpecialRegSet1, LBus2Reg0);
  and and_41 (and_41_out, SpecialRegSet1, Reg02LBus);
  and and_42 (and_42_out, SpecialRegSet1, LBus2Reg1);
  and and_43 (and_43_out, SpecialRegSet1, Reg12LBus);
  and and_44 (and_44_out, SpecialRegSet3, LBus2Reg0);
  and and_45 (and_45_out, SpecialRegSet3, Reg02LBus);
  and and_46 (and_46_out, SpecialRegSet3, LBus2Reg1);
  and and_47 (and_47_out, SpecialRegSet3, Reg12LBus);

  // Other names for the same wires on the sheet: Write_ReadPin = W_nR; BusEnablePin = BEn; AddressPort[15:0] = Adr;
  //   DataPort[7:0] = D; DMAAckPin = DMAack; IEFlag = Flags[3]; IntAckPin = IntAck; IntPin = Int;
  //   McAddrVal[11:4] = IRVal; NmiPin = Nmi; Reset = R; SyncPin = Sync

  // Notes on the sheet:
  //   DMAreq: direct memory access request
  //   Nmi: Non maskable interrupt request
  //   Int: Interrupt request
  //   D: Data port
  //   Adr: Adress
  //   R: Reset
  //   DMAack: Direct memory access acknowlege
  //   Sync: Sync goes high on Instruction fetch
  //   W_nR: High Write bus
  //   Low Read bus
  //   BEn: Bus Enable
  //   TODO:
  //    Interrupt
  //    DMA
  //    Sync
  //    Unified BusControl
  //     save some microcode space
  //   contents of eeprom_1 (hex, n*v repeats v):
  //   1,12,2,36,3,63,9,36,63,0,0,0,0,0,0,0,0,0,0,0,0,0,0,0,0,0,0,0,0,0,0,0,ac,dc
  //   contents of Fetch_Management_Code_High (hex, n*v repeats v):
  //   30c0,d8600,0,0,0,0,0,0,0,0,0,0,0,0,0,0,0,0,0,0,0,0,0,0,0,0,0,0,0,0,0,0,20610,38000,
  //   20000,0,0,0,0,0,0,0,0,0,0,0,0,0,0,0,0,0,0,0,0,0,0,0,0,0,0,0,0,0,0,0,0,0,0,0,0,0,0,
  //   0,0,0,0,0,0,0,0,0,0,0,0,0,0,0,0,0,0,0,0,0,0,0,0,0,0,0,0,0,0,0,0,0,0,0,0,0,0,0,0,0,
  //   0,0,0,0,0,0,0,0,0,0,0,0,0,0,0,0,0,0,0,0,0,0,0,0,0,0,0,0,0,0,0,0,0,0,0,0,0,0,0,0,0,
  //   0,0,0,0,0,0,0,0,0,0,0,0,0,0,0,0,0,0,0,0,0,0,0,0,0,0,0,0,0,0,0,0,0,0,0,0,0,0,0,0,0,
  //   0,0,0,0,0,0,0,0,0,0,0,0,0,0,0,0,0,0,0,0,0,0,0,0,0,0,0,0,0,0,0,0,0,0,0,0,0,0,0,0,0,
  //   0,0,0,0,0,0,0,0,0,0,0,0,0,0,0,0,0,0,0,0,0,0,0,0,0,0,0,0,0,0,0,0,0,0,0,0,0,0,0,0,0,
  //   0,0,0,0,0,0,0,0,0,0,0,0,0,0,0,0,0,0,0,0,0,0,0,0,0,0,0,0,0,0,0,0,0,0,0,0,0,0,0,0,0,
  //   0,0,0,0,0,0,0,0,0,0,0,0,0,0,0,0,0,0,0,0,0,0,0,0,0,0,0,0,0,0,0,0,0,0,0,0,0,0,0,0,0,
  //   0,0,0,0,0,0,0,0,0,0,0,0,0,0,0,0,0,0,0,0,0,0,0,0,0,0,0,0,0,0,0,0,0,0,0,0,0,0,0,0,0,
  //   0,0,0,0,0,0,0,0,0,0,0,0,0,0,0,0,0,0,0,0,0,0,0,0,0,0,0,0,0,0,0,0,0,0,0,0,0,0,0,0,0,
  //   0,0,0,0,0,0,0,0,0,0,0,0,0,0,0,0,0,0,0,0,0,0,0,0,0,0,0,0,0,0,0,0,0,0,0,0,0,0,0,0,0,
  //   0,0,0,0,0,0,0,0,0,0,0,0,0,0,0,0,0,0,0,0,0,0,0,0,0,0,0,0,0,0,0,0,0,0,0,0,0,0,0,0,0,
  //   0,0,0,0,0,0,0,0,0,0,0,0,0,0,0,0,0,0,0,0,0,0,0,0,0,0,0,0,0,0,0,0,0,0,0,0,0,0,0,0,0,
  //   0,0,0,0,0,0,0,0,0,0,0,0,0,0,0,0,0,0,0,0,0,0,0,0,0,0,0,0,0,0,0,0,0,0,0,0,0,0,0,0,0,
  //   0,0,0,0,0,0,0,0,0,0,0,0,0,0,0,0,0,0,0,0,0,0,0,0,0,0,0,0,0,0,0,0,0,0,0,0,0,0,0,0,0,
  //   0,0,0,0,0,0,0,0,0,0,0,0,0,0,0,0,0,0,0,0,0,0,0,0,0,0,0,0,0,0,0,0,0,0,0,0,0,0,0,0,0,
  //   0,0,0,0,0,0,0,0,0,0,0,0,0,0,0,0,0,0,0,0,0,0,0,0,0,0,0,0,0,0,0,0,0,0,0,0,0,0,0,0,0,
  //   0,0,0,0,0,0,0,0,0,0,0,0,0,0,0,0,0,0,0,0,0,0,0,0,0,0,0,0,0,0,0,0,0,0,0,0,0,0,0,0,0,
  //   0,0,0,0,0,0,0,0,0,0,0,0,0,0,0,0,0,0,0,0,0,0,0,0,0,0,0,0,0,0,0,0,0,0,0,0,0,0,0,0,0,
  //   0,0,0,0,0,0,0,0,0,0,0,0,0,0,0,0,0,0,0,0,0,0,0,0,0,0,0,0,0,0,0,0,0,0,0,0,0,0,0,0,0,
  //   0,0,0,0,0,0,0,0,0,0,0,0,0,0,0,0,0,0,0,0,0,0,0,0,0,0,0,0,0,0,0,0,0,0,0,0,0,0,0,0,0,
  //   0,0,0,0,0,0,0,0,0,0,0,0,0,0,0,0,0,0,0,0,0,0,0,0,0,0,0,0,0,0,0,0,0,0,0,0,0,0,0,0,0,
  //   0,0,0,0,0,0,0,0,0,0,0,0,0,0,0,0,0,0,0,0,0,0,0,0,0,0,0,0,0,0,0,0,0,0,0,0,0,0,0,0,0,
  //   0,0,0,0,0,0,0,0,0,0,0,0,0,0,0,0,0,0,0,0,0,0,0,0,0,0,0,0,0,0,0,0,0,0,0,0,0,0,0,0,0,
  //   0,0,0,0,0,0,0,0,0,0,0,0,0,0,0,0,0,0,0,0,0,0,0,0,0,0,0,0,0,0,0,0,0,0,0,0,0,0,0,0,0,
  //   0,0,0,0,0,0,0,0,0,0,0,0,0,0,0,0,0,0,0,0,0,0,0,0,0,0,0,0,0,0,0,0,0,0,0,0,0,0,0,0,0,
  //   0,0,0,0,0,0,0,0,0,0,0,0,0,0,0,0,0,0,0,0,0,0,0,0,0,0,0,0,0,0,0,0,0,0,0,0,0,0,0,0,0,
  //   0,0,0,0,0,0,0,0,0,0,0,0,0,0,0,0,0,0,0,0,0,0,0,0,0,0,0,0,0,0,0,0,0,0,0,0,0,0,0,0,0,
  //   0,0,0,0,0,0,0,0,0,0,0,0,0,0,0,0,0,0,0,0,0,0,0,0,0,0,0,0,0,0,0,0,0,0,0,0,0,0,0,0,0,
  //   0,0,0,0,0,0,0,0,0,0,0,0,0,0,0,0,0,0,0,0,0,0,0,0,0,0,0,0,0,0,0,0,0,0,0,0,0,0,0,0,0,
  //   0,0,0,0,0,0,0,0,0,0,0,0,0,0,0,0,0,0,0,0,0,0,0,0,0,0,0,0,0,0,0,0,0,0,0,0,0,0,0,0,0,
  //   0,0,0,0,0,0,0,0,0,0,0,0,0,0,0,0,0,0,0,0,0,0,0,0,0,0,0,0,0,0,0,0,0,0,0,0,0,0,0,0,0,
  //   0,0,0,0,0,0,0,0,0,0,0,0,0,0,0,0,0,0,0,0,0,0,0,0,0,0,0,0,0,0,0,0,0,0,0,0,0,0,0,0,0,
  //   0,0,0,0,0,0,0,0,0,0,0,0,0,0,0,0,0,0,0,0,0,0,0,0,0,0,0,0,0,0,0,0,0,0,0,0,0,0,0,0,0,
  //   0,0,0,0,0,0,0,0,0,0,0,0,0,0,0,0,0,0,0,0,0,0,0,0,0,0,0,0,0,0,0,0,0,0,0,0,0,0,0,0,0,
  //   0,0,0,0,0,0,0,0,0,0,0,0,0,0,0,0,0,0,0,0,0,0,0,0,0,0,0,0,0,0,0,0,0,0,0,0,0,0,0,0,0,
  //   0,0,0,0,0,0,0,0,0,0,0,0,0,0,0,0,0,0,0,0,0,0,0,0,0,0,0,0,0,0,0,0,0,0,0,0,0,0,0,0,0,
  //   0,0,0,0,0,0,0,0,0,0,0,0,0,0,0,0,0,0,0,0,0,0,0,0,0,0,0,0,0,0,0,0,0,0,0,0,0,0,0,0,0,
  //   0,0,0,0,0,0,0,0,0,0,0,0,0,0,0,0,0,0,0,0,0,0,0,0,0,0,0,0,0,0,0,0,0,0,0,0,0,0,0,0,0,
  //   0,0,0,0,0,0,0,0,0,0,0,0,0,0,0,0,0,0,0,0,0,0,0,0,0,0,0,0,0,0,0,0,0,0,0,0,0,0,0,0,0,
  //   0,0,0,0,0,0,0,0,0,0,0,0,0,0,0,0,0,0,0,0,0,0,0,0,0,0,0,0,0,0,0,0,0,0,0,0,0,0,0,0,0,
  //   0,0,0,0,0,0,0,0,0,0,0,0,0,0,0,0,0,0,0,0,0,0,0,0,0,0,0,0,0,0,0,0,0,0,0,0,0,0,0,0,0,
  //   0,0,0,0,0,0,0,0,0,0,0,0,0,0,0,0,0,0,0,0,0,0,0,0,0,0,0,0,0,0,0,0,0,0,0,0,0,0,0,0,0,
  //   0,0,0,0,0,0,0,0,0,0,0,0,0,0,0,0,0,0,0,0,0,0,0,0,0,0,0,0,0,0,0,0,0,0,0,0,0,0,0,0,0,
  //   0,0,0,0,0,0,0,0,0,0,0,0,0,0,0,0,0,0,0,0,0,0,0,0,0,0,0,0,0,0,0,0,0,0,0,0,0,0,0,0,0,
  //   0,0,0,0,0,0,0,0,0,0,0,0,0,0,0,0,0,0,0,0,0,0,0,0,0,0,0,0,0,0,0,0,0,0,0,0,0,0,0,0,0,
  //   0,0,0,0,0,0,0,0,0,0,0,0,0,0,0,0,0,0,0,0,0,0,0,0,0,0,0,0,0,0,0,0,0,0,0,0,0,0,0,0,0,
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  //   contents of Fetch_Management_Code_Low (hex, n*v repeats v):
  //   2002000,640200a,0,0,0,0,0,0,0,0,0,0,0,0,0,0,0,0,0,0,0,0,0,0,0,0,0,0,0,0,0,0,8000,
  //   8000,8,0,0,0,0,0,0,0,0,0,0,0,0,0,0,0,0,0,0,0,0,0,0,0,0,0,0,0,0,0,0,0,0,0,0,0,0,0,
  //   0,0,0,0,0,0,0,0,0,0,0,0,0,0,0,0,0,0,0,0,0,0,0,0,0,0,0,0,0,0,0,0,0,0,0,0,0,0,0,0,0,
  //   0,0,0,0,0,0,0,0,0,0,0,0,0,0,0,0,0,0,0,0,0,0,0,0,0,0,0,0,0,0,0,0,0,0,0,0,0,0,0,0,0,
  //   0,0,0,0,0,0,0,0,0,0,0,0,0,0,0,0,0,0,0,0,0,0,0,0,0,0,0,0,0,0,0,0,0,0,0,0,0,0,0,0,0,
  //   0,0,0,0,0,0,0,0,0,0,0,0,0,0,0,0,0,0,0,0,0,0,0,0,0,0,0,0,0,0,0,0,0,0,0,0,0,0,0,0,0,
  //   0,0,0,0,0,0,0,0,0,0,0,0,0,0,0,0,0,0,0,0,0,0,0,0,0,0,0,0,0,0,0,0,0,0,0,0,0,0,0,0,0,
  //   0,0,0,0,0,0,0,0,0,0,0,0,0,0,0,0,0,0,0,0,0,0,0,0,0,0,0,0,0,0,0,0,0,0,0,0,0,0,0,0,0,
  //   0,0,0,0,0,0,0,0,0,0,0,0,0,0,0,0,0,0,0,0,0,0,0,0,0,0,0,0,0,0,0,0,0,0,0,0,0,0,0,0,0,
  //   0,0,0,0,0,0,0,0,0,0,0,0,0,0,0,0,0,0,0,0,0,0,0,0,0,0,0,0,0,0,0,0,0,0,0,0,0,0,0,0,0,
  //   0,0,0,0,0,0,0,0,0,0,0,0,0,0,0,0,0,0,0,0,0,0,0,0,0,0,0,0,0,0,0,0,0,0,0,0,0,0,0,0,0,
  //   0,0,0,0,0,0,0,0,0,0,0,0,0,0,0,0,0,0,0,0,0,0,0,0,0,0,0,0,0,0,0,0,0,0,0,0,0,0,0,0,0,
  //   0,0,0,0,0,0,0,0,0,0,0,0,0,0,0,0,0,0,0,0,0,0,0,0,0,0,0,0,0,0,0,0,0,0,0,0,0,0,0,0,0,
  //   0,0,0,0,0,0,0,0,0,0,0,0,0,0,0,0,0,0,0,0,0,0,0,0,0,0,0,0,0,0,0,0,0,0,0,0,0,0,0,0,0,
  //   0,0,0,0,0,0,0,0,0,0,0,0,0,0,0,0,0,0,0,0,0,0,0,0,0,0,0,0,0,0,0,0,0,0,0,0,0,0,0,0,0,
  //   0,0,0,0,0,0,0,0,0,0,0,0,0,0,0,0,0,0,0,0,0,0,0,0,0,0,0,0,0,0,0,0,0,0,0,0,0,0,0,0,0,
  //   0,0,0,0,0,0,0,0,0,0,0,0,0,0,0,0,0,0,0,0,0,0,0,0,0,0,0,0,0,0,0,0,0,0,0,0,0,0,0,0,0,
  //   0,0,0,0,0,0,0,0,0,0,0,0,0,0,0,0,0,0,0,0,0,0,0,0,0,0,0,0,0,0,0,0,0,0,0,0,0,0,0,0,0,
  //   0,0,0,0,0,0,0,0,0,0,0,0,0,0,0,0,0,0,0,0,0,0,0,0,0,0,0,0,0,0,0,0,0,0,0,0,0,0,0,0,0,
  //   0,0,0,0,0,0,0,0,0,0,0,0,0,0,0,0,0,0,0,0,0,0,0,0,0,0,0,0,0,0,0,0,0,0,0,0,0,0,0,0,0,
  //   0,0,0,0,0,0,0,0,0,0,0,0,0,0,0,0,0,0,0,0,0,0,0,0,0,0,0,0,0,0,0,0,0,0,0,0,0,0,0,0,0,
  //   0,0,0,0,0,0,0,0,0,0,0,0,0,0,0,0,0,0,0,0,0,0,0,0,0,0,0,0,0,0,0,0,0,0,0,0,0,0,0,0,0,
  //   0,0,0,0,0,0,0,0,0,0,0,0,0,0,0,0,0,0,0,0,0,0,0,0,0,0,0,0,0,0,0,0,0,0,0,0,0,0,0,0,0,
  //   0,0,0,0,0,0,0,0,0,0,0,0,0,0,0,0,0,0,0,0,0,0,0,0,0,0,0,0,0,0,0,0,0,0,0,0,0,0,0,0,0,
  //   0,0,0,0,0,0,0,0,0,0,0,0,0,0,0,0,0,0,0,0,0,0,0,0,0,0,0,0,0,0,0,0,0,0,0,0,0,0,0,0,0,
  //   0,0,0,0,0,0,0,0,0,0,0,0,0,0,0,0,0,0,0,0,0,0,0,0,0,0,0,0,0,0,0,0,0,0,0,0,0,0,0,0,0,
  //   0,0,0,0,0,0,0,0,0,0,0,0,0,0,0,0,0,0,0,0,0,0,0,0,0,0,0,0,0,0,0,0,0,0,0,0,0,0,0,0,0,
  //   0,0,0,0,0,0,0,0,0,0,0,0,0,0,0,0,0,0,0,0,0,0,0,0,0,0,0,0,0,0,0,0,0,0,0,0,0,0,0,0,0,
  //   0,0,0,0,0,0,0,0,0,0,0,0,0,0,0,0,0,0,0,0,0,0,0,0,0,0,0,0,0,0,0,0,0,0,0,0,0,0,0,0,0,
  //   0,0,0,0,0,0,0,0,0,0,0,0,0,0,0,0,0,0,0,0,0,0,0,0,0,0,0,0,0,0,0,0,0,0,0,0,0,0,0,0,0,
  //   0,0,0,0,0,0,0,0,0,0,0,0,0,0,0,0,0,0,0,0,0,0,0,0,0,0,0,0,0,0,0,0,0,0,0,0,0,0,0,0,0,
  //   0,0,0,0,0,0,0,0,0,0,0,0,0,0,0,0,0,0,0,0,0,0,0,0,0,0,0,0,0,0,0,0,0,0,0,0,0,0,0,0,0,
  //   0,0,0,0,0,0,0,0,0,0,0,0,0,0,0,0,0,0,0,0,0,0,0,0,0,0,0,0,0,0,0,0,0,0,0,0,0,0,0,0,0,
  //   0,0,0,0,0,0,0,0,0,0,0,0,0,0,0,0,0,0,0,0,0,0,0,0,0,0,0,0,0,0,0,0,0,0,0,0,0,0,0,0,0,
  //   0,0,0,0,0,0,0,0,0,0,0,0,0,0,0,0,0,0,0,0,0,0,0,0,0,0,0,0,0,0,0,0,0,0,0,0,0,0,0,0,0,
  //   0,0,0,0,0,0,0,0,0,0,0,0,0,0,0,0,0,0,0,0,0,0,0,0,0,0,0,0,0,0,0,0,0,0,0,0,0,0,0,0,0,
  //   0,0,0,0,0,0,0,0,0,0,0,0,0,0,0,0,0,0,0,0,0,0,0,0,0,0,0,0,0,0,0,0,0,0,0,0,0,0,0,0,0,
  //   0,0,0,0,0,0,0,0,0,0,0,0,0,0,0,0,0,0,0,0,0,0,0,0,0,0,0,0,0,0,0,0,0,0,0,0,0,0,0,0,0,
  //   0,0,0,0,0,0,0,0,0,0,0,0,0,0,0,0,0,0,0,0,0,0,0,0,0,0,0,0,0,0,0,0,0,0,0,0,0,0,0,0,0,
  //   0,0,0,0,0,0,0,0,0,0,0,0,0,0,0,0,0,0,0,0,0,0,0,0,0,0,0,0,0,0,0,0,0,0,0,0,0,0,0,0,0,
  //   0,0,0,0,0,0,0,0,0,0,0,0,0,0,0,0,0,0,0,0,0,0,0,0,0,0,0,0,0,0,0,0,0,0,0,0,0,0,0,0,0,
  //   0,0,0,0,0,0,0,0,0,0,0,0,0,0,0,0,0,0,0,0,0,0,0,0,0,0,0,0,0,0,0,0,0,0,0,0,0,0,0,0,0,
  //   0,0,0,0,0,0,0,0,0,0,0,0,0,0,0,0,0,0,0,0,0,0,0,0,0,0,0,0,0,0,0,0,0,0,0,0,0,0,0,0,0,
  //   0,0,0,0,0,0,0,0,0,0,0,0,0,0,0,0,0,0,0,0,0,0,0,0,0,0,0,0,0,0,0,0,0,0,0,0,0,0,0,0,0,
  //   0,0,0,0,0,0,0,0,0,0,0,0,0,0,0,0,0,0,0,0,0,0,0,0,0,0,0,0,0,0,0,0,0,0,0,0,0,0,0,0,0,
  //   0,0,0,0,0,0,0,0,0,0,0,0,0,0,0,0,0,0,0,0,0,0,0,0,0,0,0,0,0,0,0,0,0,0,0,0,0,0,0,0,0,
  //   0,0,0,0,0,0,0,0,0,0,0,0,0,0,0,0,0,0,0,0,0,0,0,0,0,0,0,0,0,0,0,0,0,0,0,0,0,0,0,0,0,
  //   0,0,0,0,0,0,0,0,0,0,0,0,0,0,0,0,0,0,0,0,0,0,0,0,0,0,0,0,0,0,0,0,0,0,0,0,0,0,0,0,0,
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  //   contents of Fetch_Management_Code_Extended (hex, n*v repeats v):
  //   c,0,0,0,0,0,0,0,0,0,0,0,0,0,0,0,0,0,0,0,0,0,0,0,0,0,0,0,0,0,0,0,0,0,0,0,0,0,0,0,0,
  //   0,0,0,0,0,0,0,0,0,0,0,0,0,0,0,0,0,0,0,0,0,0,0,0,0,0,0,0,0,0,0,0,0,0,0,0,0,0,0,0,0,
  //   0,0,0,0,0,0,0,0,0,0,0,0,0,0,0,0,0,0,0,0,0,0,0,0,0,0,0,0,0,0,0,0,0,0,0,0,0,0,0,0,0,
  //   0,0,0,0,0,0,0,0,0,0,0,0,0,0,0,0,0,0,0,0,0,0,0,0,0,0,0,0,0,0,0,0,0,0,0,0,0,0,0,0,0,
  //   0,0,0,0,0,0,0,0,0,0,0,0,0,0,0,0,0,0,0,0,0,0,0,0,0,0,0,0,0,0,0,0,0,0,0,0,0,0,0,0,0,
  //   0,0,0,0,0,0,0,0,0,0,0,0,0,0,0,0,0,0,0,0,0,0,0,0,0,0,0,0,0,0,0,0,0,0,0,0,0,0,0,0,0,
  //   0,0,0,0,0,0,0,0,0,0,0,0,0,0,0,0,0,0,0,0,0,0,0,0,0,0,0,0,0,0,0,0,0,0,0,0,0,0,0,0,0,
  //   0,0,0,0,0,0,0,0,0,0,0,0,0,0,0,0,0,0,0,0,0,0,0,0,0,0,0,0,0,0,0,0,0,0,0,0,0,0,0,0,0,
  //   0,0,0,0,0,0,0,0,0,0,0,0,0,0,0,0,0,0,0,0,0,0,0,0,0,0,0,0,0,0,0,0,0,0,0,0,0,0,0,0,0,
  //   0,0,0,0,0,0,0,0,0,0,0,0,0,0,0,0,0,0,0,0,0,0,0,0,0,0,0,0,0,0,0,0,0,0,0,0,0,0,0,0,0,
  //   0,0,0,0,0,0,0,0,0,0,0,0,0,0,0,0,0,0,0,0,0,0,0,0,0,0,0,0,0,0,0,0,0,0,0,0,0,0,0,0,0,
  //   0,0,0,0,0,0,0,0,0,0,0,0,0,0,0,0,0,0,0,0,0,0,0,0,0,0,0,0,0,0,0,0,0,0,0,0,0,0,0,0,0,
  //   0,0,0,0,0,0,0,0,0,0,0,0,0,0,0,0,0,0,0,0,0,0,0,0,0,0,0,0,0,0,0,0,0,0,0,0,0,0,0,0,0,
  //   0,0,0,0,0,0,0,0,0,0,0,0,0,0,0,0,0,0,0,0,0,0,0,0,0,0,0,0,0,0,0,0,0,0,0,0,0,0,0,0,0,
  //   0,0,0,0,0,0,0,0,0,0,0,0,0,0,0,0,0,0,0,0,0,0,0,0,0,0,0,0,0,0,0,0,0,0,0,0,0,0,0,0,0,
  //   0,0,0,0,0,0,0,0,0,0,0,0,0,0,0,0,0,0,0,0,0,0,0,0,0,0,0,0,0,0,0,0,0,0,0,0,0,0,0,0,0,
  //   0,0,0,0,0,0,0,0,0,0,0,0,0,0,0,0,0,0,0,0,0,0,0,0,0,0,0,0,0,0,0,0,0,0,0,0,0,0,0,0,0,
  //   0,0,0,0,0,0,0,0,0,0,0,0,0,0,0,0,0,0,0,0,0,0,0,0,0,0,0,0,0,0,0,0,0,0,0,0,0,0,0,0,0,
  //   0,0,0,0,0,0,0,0,0,0,0,0,0,0,0,0,0,0,0,0,0,0,0,0,0,0,0,0,0,0,0,0,0,0,0,0,0,0,0,0,0,
  //   0,0,0,0,0,0,0,0,0,0,0,0,0,0,0,0,0,0,0,0,0,0,0,0,0,0,0,0,0,0,0,0,0,0,0,0,0,0,0,0,0,
  //   0,0,0,0,0,0,0,0,0,0,0,0,0,0,0,0,0,0,0,0,0,0,0,0,0,0,0,0,0,0,0,0,0,0,0,0,0,0,0,0,0,
  //   0,0,0,0,0,0,0,0,0,0,0,0,0,0,0,0,0,0,0,0,0,0,0,0,0,0,0,0,0,0,0,0,0,0,0,0,0,0,0,0,0,
  //   0,0,0,0,0,0,0,0,0,0,0,0,0,0,0,0,0,0,0,0,0,0,0,0,0,0,0,0,0,0,0,0,0,0,0,0,0,0,0,0,0,
  //   0,0,0,0,0,0,0,0,0,0,0,0,0,0,0,0,0,0,0,0,0,0,0,0,0,0,0,0,0,0,0,0,0,0,0,0,0,0,0,0,0,
  //   0,0,0,0,0,0,0,0,0,0,0,0,0,0,0,0,0,0,0,0,0,0,0,0,0,0,0,0,0,0,0,0,0,0,0,0,0,0,0,0,0,
  //   0,0,0,0,0,0,0,0,0,0,0,0,0,0,0,0,0,0,0,0,0,0,0,0,0,0,0,0,0,0,0,0,0,0,0,0,0,0,0,0,0,
  //   0,0,0,0,0,0,0,0,0,0,0,0,0,0,0,0,0,0,0,0,0,0,0,0,0,0,0,0,0,0,0,0,0,0,0,0,0,0,0,0,0,
  //   0,0,0,0,0,0,0,0,0,0,0,0,0,0,0,0,0,0,0,0,0,0,0,0,0,0,0,0,0,0,0,0,0,0,0,0,0,0,0,0,0,
  //   0,0,0,0,0,0,0,0,0,0,0,0,0,0,0,0,0,0,0,0,0,0,0,0,0,0,0,0,0,0,0,0,0,0,0,0,0,0,0,0,0,
  //   0,0,0,0,0,0,0,0,0,0,0,0,0,0,0,0,0,0,0,0,0,0,0,0,0,0,0,0,0,0,0,0,0,0,0,0,0,0,0,0,0,
  //   0,0,0,0,0,0,0,0,0,0,0,0,0,0,0,0,0,0,0,0,0,0,0,0,0,0,0,0,0,0,0,0,0,0,0,0,0,0,0,0,0,
  //   0,0,0,0,0,0,0,0,0,0,0,0,0,0,0,0,0,0,0,0,0,0,0,0,0,0,0,0,0,0,0,0,0,0,0,0,0,0,0,0,0,
  //   0,0,0,0,0,0,0,0,0,0,0,0,0,0,0,0,0,0,0,0,0,0,0,0,0,0,0,0,0,0,0,0,0,0,0,0,0,0,0,0,0,
  //   0,0,0,0,0,0,0,0,0,0,0,0,0,0,0,0,0,0,0,0,0,0,0,0,0,0,0,0,0,0,0,0,0,0,0,0,0,0,0,0,0,
  //   0,0,0,0,0,0,0,0,0,0,0,0,0,0,0,0,0,0,0,0,0,0,0,0,0,0,0,0,0,0,0,0,0,0,0,0,0,0,0,0,0,
  //   0,0,0,0,0,0,0,0,0,0,0,0,0,0,0,0,0,0,0,0,0,0,0,0,0,0,0,0,0,0,0,0,0,0,0,0,0,0,0,0,0,
  //   0,0,0,0,0,0,0,0,0,0,0,0,0,0,0,0,0,0,0,0,0,0,0,0,0,0,0,0,0,0,0,0,0,0,0,0,0,0,0,0,0,
  //   0,0,0,0,0,0,0,0,0,0,0,0,0,0,0,0,0,0,0,0,0,0,0,0,0,0,0,0,0,0,0,0,0,0,0,0,0,0,0,0,0,
  //   0,0,0,0,0,0,0,0,0,0,0,0,0,0,0,0,0,0,0,0,0,0,0,0,0,0,0,0,0,0,0,0,0,0,0,0,0,0,0,0,0,
  //   0,0,0,0,0,0,0,0,0,0,0,0,0,0,0,0,0,0,0,0,0,0,0,0,0,0,0,0,0,0,0,0,0,0,0,0,0,0,0,0,0,
  //   0,0,0,0,0,0,0,0,0,0,0,0,0,0,0,0,0,0,0,0,0,0,0,0,0,0,0,0,0,0,0,0,0,0,0,0,0,0,0,0,0,
  //   0,0,0,0,0,0,0,0,0,0,0,0,0,0,0,0,0,0,0,0,0,0,0,0,0,0,0,0,0,0,0,0,0,0,0,0,0,0,0,0,0,
  //   0,0,0,0,0,0,0,0,0,0,0,0,0,0,0,0,0,0,0,0,0,0,0,0,0,0,0,0,0,0,0,0,0,0,0,0,0,0,0,0,0,
  //   0,0,0,0,0,0,0,0,0,0,0,0,0,0,0,0,0,0,0,0,0,0,0,0,0,0,0,0,0,0,0,0,0,0,0,0,0,0,0,0,0,
  //   0,0,0,0,0,0,0,0,0,0,0,0,0,0,0,0,0,0,0,0,0,0,0,0,0,0,0,0,0,0,0,0,0,0,0,0,0,0,0,0,0,
  //   0,0,0,0,0,0,0,0,0,0,0,0,0,0,0,0,0,0,0,0,0,0,0,0,0,0,0,0,0,0,0,0,0,0,0,0,0,0,0,0,0,
  //   0,0,0,0,0,0,0,0,0,0,0,0,0,0,0,0,0,0,0,0,0,0,0,0,0,0,0,0,0,0,0,0,0,0,0,0,0,0,0,0,0,
  //   0,0,0,0,0,0,0,0,0,0,0,0,0,0,0,0,0,0,0,0,0,0,0,0,0,0,0,0,0,0,0,0,0,0,0,0,0,0,0,0,0,
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  //   contents of Execute_Code_High (hex, n*v repeats v):
  //   0,0,0,0,0,0,0,0,0,0,0,0,0,0,0,0,d8600,0,0,0,0,0,0,0,0,0,0,0,0,0,0,0,30c0,c0210,18600,
  //   0,0,0,0,0,0,0,0,0,0,0,0,0,30c0,c8000,18600,0,0,0,0,0,0,0,0,0,0,0,0,0,30c0,c0310,18600,
  //   0,0,0,0,0,0,0,0,0,0,0,0,0,30c0,cc000,18600,0,0,0,0,0,0,0,0,0,0,0,0,0,30c0,c0410,18600,
  //   0,0,0,0,0,0,0,0,0,0,0,0,0,30c0,d0000,18600,0,0,0,0,0,0,0,0,0,0,0,0,0,30c0,c0210,18600,
  //   c8000,0,0,0,0,0,0,0,0,0,0,0,0,30c0,c0310,18600,cc000,0,0,0,0,0,0,0,0,0,0,0,0,30c0,
  //   c0410,18600,d0000,0,0,0,0,0,0,0,0,0,0,0,0,30c0,400c0610,18600,400d8000,0,0,0,0,0,
  //   0,0,0,0,0,0,0,30c0,400c0710,18600,400dc000,0,0,0,0,0,0,0,0,0,0,0,0,30c0,c0110,18600,
  //   c0020,c0000,0,0,0,0,0,0,0,0,0,0,0,30c0,c0110,18600,c0020,c0410,d0000,0,0,0,0,0,0,
  //   0,0,0,0,1040,c0000,0,0,0,0,0,0,0,0,0,0,0,0,0,0,0,0,0,0,0,0,0,0,0,0,0,0,0,0,0,0,1860,
  //   c0000,0,0,0,0,0,0,0,0,0,0,0,0,0,0,0,0,0,0,0,0,0,0,0,0,0,0,0,0,0,0,2080,c0000,0,0,
  //   0,0,0,0,0,0,0,0,0,0,0,0,2080,c0210,0,0,0,0,0,0,0,0,0,0,0,0,0,0,2080,c8000,0,0,0,0,
  //   0,0,0,0,0,0,0,0,0,0,2080,c0310,0,0,0,0,0,0,0,0,0,0,0,0,0,0,2080,cc000,0,0,0,0,0,0,
  //   0,0,0,0,0,0,0,0,2080,c0410,0,0,0,0,0,0,0,0,0,0,0,0,0,0,2080,d0000,0,0,0,0,0,0,0,0,
  //   0,0,0,0,0,0,0,0,0,0,0,0,0,0,0,0,0,0,0,0,0,0,0,0,0,0,0,0,0,0,0,0,0,0,0,0,0,0,0,0,0,
  //   0,0,0,0,0,0,0,0,0,0,0,0,0,400030c0,c0000,0,0,0,0,0,0,0,0,0,0,0,0,0,0,0,0,0,0,0,0,
  //   0,0,0,0,0,0,0,0,0,0,0,0,0,0,0,0,0,0,0,0,0,0,0,0,0,0,0,0,0,0,0,0,0,0,0,0,0,0,0,0,0,
  //   0,0,0,0,0,0,0,0,0,0,0,0,0,0,0,0,0,0,0,0,0,0,0,0,0,0,0,0,0,0,0,0,0,0,0,0,0,0,0,0,0,
  //   0,0,0,0,0,0,0,0,0,0,0,0,0,0,0,0,0,0,0,0,0,0,0,0,400038e0,c0000,0,0,0,0,0,0,0,0,0,
  //   0,0,0,0,0,0,0,0,0,0,0,0,0,0,0,0,0,0,0,0,0,0,0,0,0,0,0,0,0,0,0,0,0,0,0,0,0,0,0,0,0,
  //   0,0,0,0,0,0,0,0,0,0,0,0,0,0,0,0,0,0,0,0,0,0,0,0,0,0,0,0,0,0,0,0,0,0,0,0,0,0,0,0,0,
  //   0,0,0,0,0,0,0,0,0,0,0,0,0,0,0,0,0,0,0,0,0,0,0,0,0,0,0,0,0,0,0,0,0,0,0,28a0,c0000,
  //   0,0,0,0,0,0,0,0,0,0,0,0,0,0,0,0,0,0,0,0,0,0,0,0,0,0,0,0,0,0,0,0,0,0,0,0,0,0,0,0,0,
  //   0,0,0,0,0,0,0,0,0,0,0,0,0,0,0,0,0,0,0,0,0,0,0,0,0,0,0,0,0,0,0,0,0,0,0,0,0,0,0,0,0,
  //   0,0,0,0,0,0,0,0,0,0,0,0,0,0,0,0,0,0,0,0,0,0,0,0,0,0,0,0,0,0,0,0,0,0,0,0,0,0,0,0,0,
  //   0,0,0,0,0,0,0,0,0,0,0,0,0,0,0,0,0,0,0,0,0,0,0,0,0,0,0,0,0,0,0,0,0,0,0,0,0,0,0,0,0,
  //   0,0,0,0,0,0,0,0,0,0,0,0,0,0,0,0,0,0,0,0,0,0,0,0,0,0,0,0,0,0,0,0,0,0,0,0,0,0,0,0,0,
  //   0,0,0,0,0,0,0,0,0,0,0,0,0,0,0,0,0,0,0,0,0,0,0,0,0,0,0,0,0,0,0,0,0,0,0,0,0,0,0,0,0,
  //   0,0,0,0,0,0,0,0,0,0,0,0,0,0,0,0,0,0,0,0,0,0,0,0,0,0,0,0,0,0,0,0,0,0,0,0,0,0,0,0,0,
  //   0,0,0,0,0,0,0,0,0,0,0,0,0,0,0,0,0,0,0,0,0,0,0,0,0,0,0,0,0,0,0,0,0,0,0,0,0,0,0,0,0,
  //   0,0,0,0,0,0,0,0,0,0,0,0,0,0,0,0,0,0,0,0,0,0,0,0,0,0,0,0,0,0,0,0,0,0,0,0,0,0,0,0,0,
  //   0,0,0,0,0,0,0,0,0,0,0,0,0,0,0,0,0,0,0,0,0,0,0,0,0,0,0,0,0,0,0,0,0,0,0,0,0,0,0,0,0,
  //   0,0,0,0,0,0,0,0,0,0,0,0,0,0,0,0,0,0,0,0,0,0,0,0,0,0,0,0,0,0,0,0,0,0,0,0,0,0,0,0,0,
  //   0,0,0,0,0,0,0,0,0,0,0,0,0,0,0,0,0,0,0,0,0,0,0,0,0,0,0,0,0,0,0,0,0,0,0,0,0,0,0,0,0,
  //   0,0,0,0,0,0,0,0,0,0,0,0,0,0,0,0,0,0,0,0,0,0,0,0,0,0,0,0,0,0,0,0,0,0,0,0,0,0,0,0,0,
  //   0,0,0,0,0,0,0,0,0,0,0,0,0,0,0,0,0,0,0,0,0,0,0,0,0,0,0,0,0,0,0,0,0,0,0,0,0,0,0,0,0,
  //   0,0,0,0,0,0,0,0,0,0,0,0,0,0,0,0,0,0,0,0,0,0,0,0,0,0,0,0,0,0,0,0,0,0,0,0,0,0,0,0,0,
  //   0,0,0,0,0,0,0,0,0,0,0,0,0,0,0,0,0,0,0,0,0,0,0,0,0,0,0,0,0,0,0,0,0,0,0,0,0,0,0,0,0,
  //   0,0,0,0,0,0,0,0,0,0,0,0,0,0,0,0,0,0,0,0,0,0,0,0,0,0,0,0,0,0,0,0,0,0,0,0,0,0,0,0,0,
  //   0,0,0,0,0,0,0,0,0,0,0,0,0,0,0,0,0,0,0,0,0,0,0,0,0,0,0,0,0,0,0,0,0,0,0,0,0,0,0,0,0,
  //   0,0,0,0,0,0,0,0,0,0,0,0,0,0,0,0,0,0,0,0,0,0,0,0,0,0,0,0,0,0,0,0,0,0,0,0,0,0,0,0,0,
  //   0,0,0,0,0,0,0,0,0,0,0,0,0,0,0,0,0,0,0,0,0,0,0,0,0,0,0,0,0,0,0,0,0,0,0,0,0,0,0,0,0,
  //   0,0,0,0,0,0,0,0,0,0,0,0,0,0,0,0,0,0,0,0,0,0,0,0,0,0,0,0,0,0,0,0,0,0,0,0,0,0,0,0,0,
  //   0,0,0,0,0,0,0,0,0,0,0,0,0,0,0,0,0,0,0,0,0,0,0,0,0,0,0,0,0,0,0,0,0,0,0,0,0,0,0,0,0,
  //   0,0,0,0,0,0,0,0,0,0,0,0,0,0,0,0,0,0,0,0,0,0,0,0,0,0,0,0,0,0,0,0,0,0,0,0,0,0,0,0,0,
  //   0,0,0,0,0,0,0,0,0,0,0,0,0,0,0,0,0,0,0,0,0,0,0,0,0,0,0,0,0,0,0,0,0,0,0,0,0,0,0,0,0,
  //   0,0,0,0,0,0,0,0,0,0,0,0,0,0,0,0,0,0,0,0,0,0,0,0,0,0,0,0,0,0,0,0,0,0,0,0,0,0,0,0,0,
  //   0,0,0,0,0,0,0,0,0,0,0,0,0,0,0,0,0,0,0,0,0,0,0,0,0,0,0,0,0,0,0,0,0,0,0,0,0,0,0,0,0,
  //   0,0,0,0,0,0,0,0,0,0,0,0,0,0,0,0,0,0,0,0,0,0,0,0,0,0,0,0,0,0,0,0,0,0,0,0,0,0,0,0,0,
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  //   contents of Execute_Code_Low (hex, n*v repeats v):
  //   8,0,0,0,0,0,0,0,0,0,0,0,0,0,0,0,41010a,0,0,0,0,0,0,0,0,0,0,0,0,0,0,0,2002000,8002,
  //   400008,0,0,0,0,0,0,0,0,0,0,0,0,0,2002000,8002,400008,0,0,0,0,0,0,0,0,0,0,0,0,0,2002000,
  //   8002,400008,0,0,0,0,0,0,0,0,0,0,0,0,0,2002000,8002,400008,0,0,0,0,0,0,0,0,0,0,0,0,
  //   0,2002000,8002,400008,0,0,0,0,0,0,0,0,0,0,0,0,0,2002000,8002,400008,0,0,0,0,0,0,0,
  //   0,0,0,0,0,0,2002000,600a002,1400002,808008,0,0,0,0,0,0,0,0,0,0,0,0,2002000,600a002,
  //   1400002,808008,0,0,0,0,0,0,0,0,0,0,0,0,2002000,600a002,1400002,808008,0,0,0,0,0,0,
  //   0,0,0,0,0,0,2002000,600a002,1400002,808008,0,0,0,0,0,0,0,0,0,0,0,0,2002000,600a002,
  //   1400002,808008,0,0,0,0,0,0,0,0,0,0,0,0,2002000,600a002,1400002,2808000,1010a,0,0,
  //   0,0,0,0,0,0,0,0,0,2002000,600a002,1400002,280a000,6008002,800a,0,0,0,0,0,0,0,0,0,
  //   0,2000000,1010a,0,0,0,0,0,0,0,0,0,0,0,0,0,0,0,0,0,0,0,0,0,0,0,0,0,0,0,0,0,0,2000000,
  //   1010a,0,0,0,0,0,0,0,0,0,0,0,0,0,0,0,0,0,0,0,0,0,0,0,0,0,0,0,0,0,0,2000000,1010a,0,
  //   0,0,0,0,0,0,0,0,0,0,0,0,0,2000000,800a,0,0,0,0,0,0,0,0,0,0,0,0,0,0,2000000,800a,0,
  //   0,0,0,0,0,0,0,0,0,0,0,0,0,2000000,800a,0,0,0,0,0,0,0,0,0,0,0,0,0,0,2000000,800a,0,
  //   0,0,0,0,0,0,0,0,0,0,0,0,0,2000000,800a,0,0,0,0,0,0,0,0,0,0,0,0,0,0,2000000,800a,0,
  //   0,0,0,0,0,0,0,0,0,0,0,0,0,8,0,0,0,0,0,0,0,0,0,0,0,0,0,0,0,8,0,0,0,0,0,0,0,0,0,0,0,
  //   0,0,0,0,8,0,0,0,0,0,0,0,0,0,0,0,0,0,0,0,2000000,1010a,0,0,0,0,0,0,0,0,0,0,0,0,0,0,
  //   8,0,0,0,0,0,0,0,0,0,0,0,0,0,0,0,8,0,0,0,0,0,0,0,0,0,0,0,0,0,0,0,8,0,0,0,0,0,0,0,0,
  //   0,0,0,0,0,0,0,8,0,0,0,0,0,0,0,0,0,0,0,0,0,0,0,8,0,0,0,0,0,0,0,0,0,0,0,0,0,0,0,8,0,
  //   0,0,0,0,0,0,0,0,0,0,0,0,0,0,8,0,0,0,0,0,0,0,0,0,0,0,0,0,0,0,2000000,1010a,0,0,0,0,
  //   0,0,0,0,0,0,0,0,0,0,8,0,0,0,0,0,0,0,0,0,0,0,0,0,0,0,8,0,0,0,0,0,0,0,0,0,0,0,0,0,0,
  //   0,8,0,0,0,0,0,0,0,0,0,0,0,0,0,0,0,8,0,0,0,0,0,0,0,0,0,0,0,0,0,0,0,8,0,0,0,0,0,0,0,
  //   0,0,0,0,0,0,0,0,8,0,0,0,0,0,0,0,0,0,0,0,0,0,0,0,8,0,0,0,0,0,0,0,0,0,0,0,0,0,0,0,2000000,
  //   1010a,0,0,0,0,0,0,0,0,0,0,0,0,0,0,8,0,0,0,0,0,0,0,0,0,0,0,0,0,0,0,8,0,0,0,0,0,0,0,
  //   0,0,0,0,0,0,0,0,8,0,0,0,0,0,0,0,0,0,0,0,0,0,0,0,8,0,0,0,0,0,0,0,0,0,0,0,0,0,0,0,8,
  //   0,0,0,0,0,0,0,0,0,0,0,0,0,0,0,8,0,0,0,0,0,0,0,0,0,0,0,0,0,0,0,8,0,0,0,0,0,0,0,0,0,
  //   0,0,0,0,0,0,8,0,0,0,0,0,0,0,0,0,0,0,0,0,0,0,8,0,0,0,0,0,0,0,0,0,0,0,0,0,0,0,8,0,0,
  //   0,0,0,0,0,0,0,0,0,0,0,0,0,8,0,0,0,0,0,0,0,0,0,0,0,0,0,0,0,8,0,0,0,0,0,0,0,0,0,0,0,
  //   0,0,0,0,8,0,0,0,0,0,0,0,0,0,0,0,0,0,0,0,8,0,0,0,0,0,0,0,0,0,0,0,0,0,0,0,8,0,0,0,0,
  //   0,0,0,0,0,0,0,0,0,0,0,8,0,0,0,0,0,0,0,0,0,0,0,0,0,0,0,8,0,0,0,0,0,0,0,0,0,0,0,0,0,
  //   0,0,8,0,0,0,0,0,0,0,0,0,0,0,0,0,0,0,8,0,0,0,0,0,0,0,0,0,0,0,0,0,0,0,8,0,0,0,0,0,0,
  //   0,0,0,0,0,0,0,0,0,8,0,0,0,0,0,0,0,0,0,0,0,0,0,0,0,8,0,0,0,0,0,0,0,0,0,0,0,0,0,0,0,
  //   8,0,0,0,0,0,0,0,0,0,0,0,0,0,0,0,8,0,0,0,0,0,0,0,0,0,0,0,0,0,0,0,8,0,0,0,0,0,0,0,0,
  //   0,0,0,0,0,0,0,8,0,0,0,0,0,0,0,0,0,0,0,0,0,0,0,8,0,0,0,0,0,0,0,0,0,0,0,0,0,0,0,8,0,
  //   0,0,0,0,0,0,0,0,0,0,0,0,0,0,8,0,0,0,0,0,0,0,0,0,0,0,0,0,0,0,8,0,0,0,0,0,0,0,0,0,0,
  //   0,0,0,0,0,8,0,0,0,0,0,0,0,0,0,0,0,0,0,0,0,8,0,0,0,0,0,0,0,0,0,0,0,0,0,0,0,8,0,0,0,
  //   0,0,0,0,0,0,0,0,0,0,0,0,8,0,0,0,0,0,0,0,0,0,0,0,0,0,0,0,8,0,0,0,0,0,0,0,0,0,0,0,0,
  //   0,0,0,8,0,0,0,0,0,0,0,0,0,0,0,0,0,0,0,8,0,0,0,0,0,0,0,0,0,0,0,0,0,0,0,8,0,0,0,0,0,
  //   0,0,0,0,0,0,0,0,0,0,8,0,0,0,0,0,0,0,0,0,0,0,0,0,0,0,8,0,0,0,0,0,0,0,0,0,0,0,0,0,0,
  //   0,8,0,0,0,0,0,0,0,0,0,0,0,0,0,0,0,8,0,0,0,0,0,0,0,0,0,0,0,0,0,0,0,8,0,0,0,0,0,0,0,
  //   0,0,0,0,0,0,0,0,8,0,0,0,0,0,0,0,0,0,0,0,0,0,0,0,8,0,0,0,0,0,0,0,0,0,0,0,0,0,0,0,8,
  //   0,0,0,0,0,0,0,0,0,0,0,0,0,0,0,8,0,0,0,0,0,0,0,0,0,0,0,0,0,0,0,8,0,0,0,0,0,0,0,0,0,
  //   0,0,0,0,0,0,8,0,0,0,0,0,0,0,0,0,0,0,0,0,0,0,8,0,0,0,0,0,0,0,0,0,0,0,0,0,0,0,8,0,0,
  //   0,0,0,0,0,0,0,0,0,0,0,0,0,8,0,0,0,0,0,0,0,0,0,0,0,0,0,0,0,8,0,0,0,0,0,0,0,0,0,0,0,
  //   0,0,0,0,8,0,0,0,0,0,0,0,0,0,0,0,0,0,0,0,8,0,0,0,0,0,0,0,0,0,0,0,0,0,0,0,8,0,0,0,0,
  //   0,0,0,0,0,0,0,0,0,0,0,8,0,0,0,0,0,0,0,0,0,0,0,0,0,0,0,8,0,0,0,0,0,0,0,0,0,0,0,0,0,
  //   0,0,8,0,0,0,0,0,0,0,0,0,0,0,0,0,0,0,8,0,0,0,0,0,0,0,0,0,0,0,0,0,0,0,8,0,0,0,0,0,0,
  //   0,0,0,0,0,0,0,0,0,8,0,0,0,0,0,0,0,0,0,0,0,0,0,0,0,8,0,0,0,0,0,0,0,0,0,0,0,0,0,0,0,
  //   8,0,0,0,0,0,0,0,0,0,0,0,0,0,0,0,8,0,0,0,0,0,0,0,0,0,0,0,0,0,0,0,8,0,0,0,0,0,0,0,0,
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  //   contents of Execute_Code_Extended (hex, n*v repeats v):
  //   0,0,0,0,0,0,0,0,0,0,0,0,0,0,0,0,0,0,0,0,0,0,0,0,0,0,0,0,0,0,0,0,0,0,0,0,0,0,0,0,0,
  //   0,0,0,0,0,0,0,0,0,0,0,0,0,0,0,0,0,0,0,0,0,0,0,0,0,0,0,0,0,0,0,0,0,0,0,0,0,0,0,0,0,
  //   0,0,0,0,0,0,0,0,0,0,0,0,0,0,0,0,0,0,0,0,0,0,0,0,0,0,0,0,0,0,0,0,0,0,0,0,0,0,0,0,0,
  //   0,0,0,0,0,0,0,0,0,0,0,0,0,0,0,0,0,0,0,0,0,0,0,0,0,0,0,0,0,0,0,0,0,0,0,0,0,0,0,0,0,
  //   0,0,0,0,0,0,0,0,0,0,0,0,0,0,0,0,0,0,0,0,0,0,0,0,0,0,0,0,0,0,0,0,0,0,0,0,0,0,0,0,0,
  //   0,0,0,0,0,0,0,0,0,0,0,0,0,0,0,0,0,0,0,0,0,0,0,0,0,0,0,0,0,0,0,0,0,0,0,0,0,0,0,0,0,
  //   0,0,0,0,0,0,0,0,0,0,0,0,0,0,0,0,0,0,0,0,0,0,0,0,0,0,0,0,0,0,0,0,0,0,0,0,0,0,0,0,0,
  //   0,0,0,0,0,0,0,0,0,0,0,0,0,0,0,0,0,0,0,0,0,0,0,0,0,0,0,0,0,0,0,0,0,0,0,0,0,0,0,0,0,
  //   0,0,0,0,0,0,0,0,0,0,0,0,0,0,0,0,0,0,0,0,0,0,0,0,0,0,0,0,0,0,0,0,0,0,0,0,0,0,0,0,0,
  //   0,0,0,0,0,0,0,0,0,0,0,0,0,0,0,0,0,0,0,0,0,0,0,0,0,0,0,0,0,0,0,0,0,0,0,0,0,0,0,0,0,
  //   0,0,0,0,0,0,0,0,0,0,0,0,0,0,0,0,0,0,0,0,0,0,0,0,0,0,0,0,0,0,0,0,0,0,0,0,0,0,0,0,0,
  //   0,0,0,0,0,0,0,0,0,0,0,0,0,0,0,0,0,0,0,0,0,0,0,0,0,0,0,0,0,0,0,0,0,0,0,0,0,0,0,0,0,
  //   0,0,0,0,0,0,0,0,0,0,0,0,0,0,0,0,0,0,0,0,0,0,0,0,0,0,0,0,0,0,0,0,0,0,0,0,0,0,0,0,0,
  //   0,0,0,0,0,0,0,0,0,0,0,0,0,0,0,0,0,0,0,0,0,0,0,0,0,0,0,0,0,0,0,0,0,0,0,0,0,0,0,0,0,
  //   0,0,0,0,0,0,0,0,0,0,0,0,0,0,0,0,0,0,0,0,0,0,0,0,0,0,0,0,0,0,0,0,0,0,0,0,0,0,0,0,0,
  //   0,0,0,0,0,0,0,0,0,0,0,0,0,0,0,0,0,0,0,0,0,0,0,0,0,0,0,0,0,0,0,0,0,0,0,0,0,0,0,0,0,
  //   0,0,0,0,0,0,0,0,0,0,0,0,0,0,0,0,0,0,0,0,0,0,0,0,0,0,0,0,0,0,0,0,0,0,0,0,0,0,0,0,0,
  //   0,0,0,0,0,0,0,0,0,0,0,0,0,0,0,0,0,0,0,0,0,0,0,0,0,0,0,0,0,0,0,0,0,0,0,0,0,0,0,0,0,
  //   0,0,0,0,0,0,0,0,0,0,0,0,0,0,0,0,0,0,0,0,0,0,0,0,0,0,0,0,0,0,0,0,0,0,0,0,0,0,0,0,0,
  //   0,0,0,0,0,0,0,0,0,0,0,0,0,0,0,0,0,0,0,0,0,0,0,0,0,0,0,0,0,0,0,0,0,0,0,0,0,0,0,0,0,
  //   0,0,0,0,0,0,0,0,0,0,0,0,0,0,0,0,0,0,0,0,0,0,0,0,0,0,0,0,0,0,0,0,0,0,0,0,0,0,0,0,0,
  //   0,0,0,0,0,0,0,0,0,0,0,0,0,0,0,0,0,0,0,0,0,0,0,0,0,0,0,0,0,0,0,0,0,0,0,0,0,0,0,0,0,
  //   0,0,0,0,0,0,0,0,0,0,0,0,0,0,0,0,0,0,0,0,0,0,0,0,0,0,0,0,0,0,0,0,0,0,0,0,0,0,0,0,0,
  //   0,0,0,0,0,0,0,0,0,0,0,0,0,0,0,0,0,0,0,0,0,0,0,0,0,0,0,0,0,0,0,0,0,0,0,0,0,0,0,0,0,
  //   0,0,0,0,0,0,0,0,0,0,0,0,0,0,0,0,0,0,0,0,0,0,0,0,0,0,0,0,0,0,0,0,0,0,0,0,0,0,0,0,0,
  //   0,0,0,0,0,0,0,0,0,0,0,0,0,0,0,0,0,0,0,0,0,0,0,0,0,0,0,0,0,0,0,0,0,0,0,0,0,0,0,0,0,
  //   0,0,0,0,0,0,0,0,0,0,0,0,0,0,0,0,0,0,0,0,0,0,0,0,0,0,0,0,0,0,0,0,0,0,0,0,0,0,0,0,0,
  //   0,0,0,0,0,0,0,0,0,0,0,0,0,0,0,0,0,0,0,0,0,0,0,0,0,0,0,0,0,0,0,0,0,0,0,0,0,0,0,0,0,
  //   0,0,0,0,0,0,0,0,0,0,0,0,0,0,0,0,0,0,0,0,0,0,0,0,0,0,0,0,0,0,0,0,0,0,0,0,0,0,0,0,0,
  //   0,0,0,0,0,0,0,0,0,0,0,0,0,0,0,0,0,0,0,0,0,0,0,0,0,0,0,0,0,0,0,0,0,0,0,0,0,0,0,0,0,
  //   0,0,0,0,0,0,0,0,0,0,0,0,0,0,0,0,0,0,0,0,0,0,0,0,0,0,0,0,0,0,0,0,0,0,0,0,0,0,0,0,0,
  //   0,0,0,0,0,0,0,0,0,0,0,0,0,0,0,0,0,0,0,0,0,0,0,0,0,0,0,0,0,0,0,0,0,0,0,0,0,0,0,0,0,
  //   0,0,0,0,0,0,0,0,0,0,0,0,0,0,0,0,0,0,0,0,0,0,0,0,0,0,0,0,0,0,0,0,0,0,0,0,0,0,0,0,0,
  //   0,0,0,0,0,0,0,0,0,0,0,0,0,0,0,0,0,0,0,0,0,0,0,0,0,0,0,0,0,0,0,0,0,0,0,0,0,0,0,0,0,
  //   0,0,0,0,0,0,0,0,0,0,0,0,0,0,0,0,0,0,0,0,0,0,0,0,0,0,0,0,0,0,0,0,0,0,0,0,0,0,0,0,0,
  //   0,0,0,0,0,0,0,0,0,0,0,0,0,0,0,0,0,0,0,0,0,0,0,0,0,0,0,0,0,0,0,0,0,0,0,0,0,0,0,0,0,
  //   0,0,0,0,0,0,0,0,0,0,0,0,0,0,0,0,0,0,0,0,0,0,0,0,0,0,0,0,0,0,0,0,0,0,0,0,0,0,0,0,0,
  //   0,0,0,0,0,0,0,0,0,0,0,0,0,0,0,0,0,0,0,0,0,0,0,0,0,0,0,0,0,0,0,0,0,0,0,0,0,0,0,0,0,
  //   0,0,0,0,0,0,0,0,0,0,0,0,0,0,0,0,0,0,0,0,0,0,0,0,0,0,0,0,0,0,0,0,0,0,0,0,0,0,0,0,0,
  //   0,0,0,0,0,0,0,0,0,0,0,0,0,0,0,0,0,0,0,0,0,0,0,0,0,0,0,0,0,0,0,0,0,0,0,0,0,0,0,0,0,
  //   0,0,0,0,0,0,0,0,0,0,0,0,0,0,0,0,0,0,0,0,0,0,0,0,0,0,0,0,0,0,0,0,0,0,0,0,0,0,0,0,0,
  //   0,0,0,0,0,0,0,0,0,0,0,0,0,0,0,0,0,0,0,0,0,0,0,0,0,0,0,0,0,0,0,0,0,0,0,0,0,0,0,0,0,
  //   0,0,0,0,0,0,0,0,0,0,0,0,0,0,0,0,0,0,0,0,0,0,0,0,0,0,0,0,0,0,0,0,0,0,0,0,0,0,0,0,0,
  //   0,0,0,0,0,0,0,0,0,0,0,0,0,0,0,0,0,0,0,0,0,0,0,0,0,0,0,0,0,0,0,0,0,0,0,0,0,0,0,0,0,
  //   0,0,0,0,0,0,0,0,0,0,0,0,0,0,0,0,0,0,0,0,0,0,0,0,0,0,0,0,0,0,0,0,0,0,0,0,0,0,0,0,0,
  //   0,0,0,0,0,0,0,0,0,0,0,0,0,0,0,0,0,0,0,0,0,0,0,0,0,0,0,0,0,0,0,0,0,0,0,0,0,0,0,0,0,
  //   0,0,0,0,0,0,0,0,0,0,0,0,0,0,0,0,0,0,0,0,0,0,0,0,0,0,0,0,0,0,0,0,0,0,0,0,0,0,0,0,0,
  //   0,0,0,0,0,0,0,0,0,0,0,0,0,0,0,0,0,0,0,0,0,0,0,0,0,0,0,0,0,0,0,0,0,0,0,0,0,0,0,0,0,
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endmodule
